# Fritzing sketch Petrol_pump (saved by Fritzing 0.9.3b)
breadboards: 1

parts:
  Raspberry_Pi_1 = Raspberry Pi 3 [part_number=RPI-3-V1.2]
  S1 = Round Pushbutton
  S2 = Round Pushbutton
  S3 = Round Pushbutton

nets:
  3V3: Raspberry_Pi_1.3v3, Raspberry_Pi_1.5V, S1.leg0, S2.leg0, S3.leg0
  N1: Raspberry_Pi_1.GPIO18, S3.leg1
  N2: Raspberry_Pi_1.GPIO15, S2.leg1
  N3: Raspberry_Pi_1.GPIO14, S1.leg1

notes:
  Other Terminal of Sensor is connected to Pin8, Pin10 and Pin12
